# Fritzing sketch arduino esp8266 blynk (saved by Fritzing 0.9.3b)

parts:
  U1 = ESP8266 WiFi Module [part_number=ESP8266]
  Part1 = Arduino Uno (Rev3)
  R1 = Resistor [tolerance=±5% resistance=220 package=THT]
  LED1 = LEDs [package=led10mm]
  U2 = POT [package=pot_mammoth]

nets:
  N1: U1.RXD, Part1.D3_PWM
  N2: U1.CH_PD, Part1.3V3
  GND: U1.GND, Part1.GND
  N3: U1.TXD, Part1.D2
  N4: Part1.A0, U2.A
  N5: Part1.5V, U2.S
  N6: R1.Pin_1, LED1.C

custom parts:
  ESP8266 WiFi Module: Generic WiFi Module based on the ESP8266 with onboard PCB antenna and UART communications
